# Fritzing sketch I2C (saved by Fritzing 0.9.3b)
breadboards: 1

parts:
  パーツ1 = Arduino Uno (Rev3)
  Raspberry_Pi_1 = Raspberry Pi 3 [part_number=RPI-3-V1.2]
  R1 = Resistor [tolerance=±5% resistance=4.7k package=THT]
  R2 = Resistor [tolerance=±5% resistance=4.7k package=THT]

nets:
  GND: パーツ1.GND, Raspberry_Pi_1.GND
  N1: パーツ1.AREF, Raspberry_Pi_1.GPIO3, R1.Pin_0
  N2: パーツ1.A4/SDA, Raspberry_Pi_1.GPIO4, R2.Pin_0
  N3: Raspberry_Pi_1.3v3, R1.Pin_1, R2.Pin_1
