# Fritzing sketch SPI (saved by Fritzing 0.9.3b)
breadboards: 1

parts:
  パーツ1 = Arduino Uno (Rev3)
  Raspberry_Pi_1 = Raspberry Pi 3 [part_number=RPI-3-V1.2]
  R1 = Resistor [tolerance=±5% resistance=10k package=THT]
  R2 = Resistor [tolerance=±5% resistance=10k package=THT]

nets:
  N1: パーツ1.D10_PWM/SS, Raspberry_Pi_1.GPIO8
  N2: パーツ1.D11_PWM/MOSI, Raspberry_Pi_1.GPIO10
  N3: パーツ1.D12/MISO, R1.Pin_0
  N4: パーツ1.D13/SCK, Raspberry_Pi_1.GPIO11
  GND: パーツ1.GND, Raspberry_Pi_1.GND, R2.Pin_1
  N5: Raspberry_Pi_1.GPIO9, R1.Pin_1, R2.Pin_0
